# Fritzing sketch ktinga (saved by Fritzing 0.9.4)
breadboards: 1

parts:
  U1 = attiny85 [package=dip]
  LED1 = smd LED [color="Red (633nm)" package="0805 [SMD]"]
  R2 = Resistor [tolerance=±5% resistance=100 package="0402 [SMD]"]
  R3 = Resistor [tolerance=±5% resistance=100 package="0402 [SMD]"]
  LED2 = smd LED [color="Red (633nm)" package="0805 [SMD]"]
  LED3 = smd LED [color="White (8000K)" package="0805 [SMD]"]
  R4 = Resistor [tolerance=±5% resistance=100 package="0402 [SMD]"]
  LED4 = smd LED [color="White (8000K)" package="0805 [SMD]"]
  R5 = Resistor [tolerance=±5% resistance=100 package="0402 [SMD]"]

nets:
  N1: U1.Pin_2, R5.Pin_1
  N2: U1.Pin_3, R4.Pin_1
  N3: U1.Pin_4, LED3.anode, LED4.anode
  N4: U1.Pin_5, R3.Pin_0
  N5: U1.Pin_6, R2.Pin_0
  N6: LED1.cathode, R2.Pin_1
  N7: LED1.anode, LED2.anode
  N8: R3.Pin_1, LED2.cathode
  N9: LED3.cathode, R4.Pin_0
  N10: LED4.cathode, R5.Pin_0
